# Fritzing sketch M2.1_Controled_LED_Blink (saved by Fritzing 0.8.7b)
breadboards: 1

parts:
  R2 = Resistor [tolerance=±5% resistance=220 package=THT]
  LED1 = LED - 5mm [color="Red (633nm)" package="5 mm [THT]"]
  Intel(R)_Galileo_1 = Intel(R) Galileo
  R3 = TRIMPOT [package=3386u]

nets:
  N1: R2.Pin_0, LED1.anode
  N2: R2.Pin_1, Intel(R)_Galileo_1.GND, R3.CCW
  N3: LED1.cathode, Intel(R)_Galileo_1.D8
  N4: Intel(R)_Galileo_1.A0, R3.WIPER
  N5: Intel(R)_Galileo_1.5V, R3.CW

custom parts:
  Intel(R) Galileo: Galileo is a microcontroller board based on the Intel® Quark SoC X1000 Application Processor, a 32-bit Intel Pentium-class system on a chip (datasheet). It’s the first board based on Intel® architecture designed to be hardware and software pin-compatible with Arduino shields designed for the Uno R3. Digital pins 0 to 13 (and the adjacent AREF and GND pins), Analog inputs 0 to 5, the power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
