# Fritzing sketch M4.1_Pot_Controlled-Servo (saved by Fritzing 0.8.7b)
breadboards: 1

parts:
  J1 = Basic Servo [part_number=SG90]
  Potentiometer_Controlled_Servo = Intel(R) Galileo
  R2 = TRIMPOT [package=3386u]

nets:
  GND: J1.gnd, Potentiometer_Controlled_Servo.GND, R2.CCW
  VCC: J1.vcc, Potentiometer_Controlled_Servo.5V, R2.CW
  N1: J1.pulse, Potentiometer_Controlled_Servo.D9_PWM
  N2: Potentiometer_Controlled_Servo.A0, R2.WIPER

custom parts:
  Intel(R) Galileo: Galileo is a microcontroller board based on the Intel® Quark SoC X1000 Application Processor, a 32-bit Intel Pentium-class system on a chip (datasheet). It’s the first board based on Intel® architecture designed to be hardware and software pin-compatible with Arduino shields designed for the Uno R3. Digital pins 0 to 13 (and the adjacent AREF and GND pins), Analog inputs 0 to 5, the power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
